// Logisim project lab2_assingment.circ as structural Verilog: 4 circuits, main circuit main
module main (
  input  SW0,
  input  SW1,
  input  SW2,
  input  SW3,
  input  SW4,
  input  SW5,
  input  SW6,
  input  SW7,
  input  BTNR,
  output LD0,
  output LD1,
  output LD2,
  output LD3,
  output LD4
);

  FourBitFullAdder FourBitFullAdder_1 (
    .A0(SW0), .B0(SW4), .Cin(BTNR), .A1(SW1), .B1(SW5), .A2(SW2), .B2(SW6), .A3(SW3), .B3(SW7), .S0(LD0),
    .S1(LD1), .S2(LD2), .S3(LD3), .Cout(LD4));
endmodule

module HalfAdder (
  input  A,
  input  B,
  output S,
  output Cout
);

  xor xor_1 (S, A, B);
  and and_1 (Cout, A, B);
endmodule

module OneBitFullAdder (
  input  A,
  input  B,
  input  Cin,
  output S,
  output Cout
);

  wire HalfAdder_1_cout, HalfAdder_1_s, HalfAdder_2_cout;

  HalfAdder HalfAdder_1 (.A(A), .B(B), .S(HalfAdder_1_s), .Cout(HalfAdder_1_cout));
  HalfAdder HalfAdder_2 (.A(HalfAdder_1_s), .B(Cin), .S(S), .Cout(HalfAdder_2_cout));
  or or_1 (Cout, HalfAdder_1_cout, HalfAdder_2_cout);

  // Notes on the sheet:
  //   S = A⊕B⊕CIN
  //   COUT = C1 + C2
endmodule

module FourBitFullAdder (
  input  A0,
  input  B0,
  input  Cin,
  input  A1,
  input  B1,
  input  A2,
  input  B2,
  input  A3,
  input  B3,
  output S0,
  output S1,
  output S2,
  output S3,
  output Cout
);

  wire FA0_cout, FA1_cout, FA2_cout;

  OneBitFullAdder FA0 (.A(A0), .B(B0), .Cin(Cin), .S(S0), .Cout(FA0_cout));
  OneBitFullAdder FA1 (.A(A1), .B(B1), .Cin(FA0_cout), .S(S1), .Cout(FA1_cout));
  OneBitFullAdder FA2 (.A(A2), .B(B2), .Cin(FA1_cout), .S(S2), .Cout(FA2_cout));
  OneBitFullAdder FA3 (.A(A3), .B(B3), .Cin(FA2_cout), .S(S3), .Cout(Cout));
endmodule
