// Logisim project SevenSegmentDecoder.circ as structural Verilog: 3 circuits, main circuit main
module main (
  input  a,
  input  b,
  input  c,
  input  d,
  output sa,
  output sb,
  output sc,
  output sd,
  output se,
  output sf,
  output sg
);

  wire and_1_out, and_2_out, and_3_out, and_4_out, and_5_out, and_6_out, and_7_out, and_8_out, and_9_out,
       and_10_out, and_11_out, and_12_out, and_13_out, not_1_out, not_2_out, not_3_out;

  not not_1 (not_1_out, b);
  not not_2 (not_2_out, c);
  not not_3 (not_3_out, d);
  and and_1 (and_1_out, b, d);
  and and_2 (and_2_out, not_1_out, not_3_out);
  and and_3 (and_3_out, c, d);
  and and_4 (and_4_out, not_2_out, not_3_out);
  or or_1 (sc, b, d, not_2_out);
  and and_5 (and_5_out, c, not_1_out);
  and and_6 (and_6_out, c, not_3_out);
  and and_7 (and_7_out, not_1_out, not_3_out);
  and and_8 (and_8_out, b, d, not_2_out);
  and and_9 (and_9_out, c, not_3_out);
  and and_10 (and_10_out, not_1_out, not_3_out);
  and and_11 (and_11_out, b, not_2_out);
  and and_12 (and_12_out, b, not_3_out);
  and and_13 (and_13_out, not_2_out, not_3_out);
  or or_2 (sa, a, c, and_1_out, and_2_out);
  or or_3 (sb, not_1_out, and_3_out, and_4_out);
  or or_4 (sd, a, and_5_out, and_6_out, and_7_out, and_8_out);
  or or_5 (se, and_9_out, and_10_out);
  or or_6 (sf, a, and_11_out, and_12_out, and_13_out);

  assign sg = 1'b0;
endmodule

module SevenSeg (
  input  a,
  input  b,
  input  c,
  input  d,
  output sa,
  output sb,
  output sc,
  output sd,
  output se,
  output sf,
  output sg
);

  wire and_1_out, and_2_out, and_3_out, and_4_out, and_5_out, and_6_out, and_7_out, and_8_out, and_9_out,
       and_10_out, and_11_out, and_12_out, and_13_out, not_1_out, not_2_out, not_3_out;

  not not_1 (not_1_out, b);
  not not_2 (not_2_out, c);
  not not_3 (not_3_out, d);
  and and_1 (and_1_out, b, d);
  and and_2 (and_2_out, not_1_out, not_3_out);
  and and_3 (and_3_out, c, d);
  and and_4 (and_4_out, not_2_out, not_3_out);
  or or_1 (sc, b, d, not_2_out);
  and and_5 (and_5_out, c, not_1_out);
  and and_6 (and_6_out, c, not_3_out);
  and and_7 (and_7_out, not_1_out, not_3_out);
  and and_8 (and_8_out, b, d, not_2_out);
  and and_9 (and_9_out, c, not_3_out);
  and and_10 (and_10_out, not_1_out, not_3_out);
  and and_11 (and_11_out, b, not_2_out);
  and and_12 (and_12_out, b, not_3_out);
  and and_13 (and_13_out, not_2_out, not_3_out);
  or or_2 (sa, a, c, and_1_out, and_2_out);
  or or_3 (sb, not_1_out, and_3_out, and_4_out);
  or or_4 (sd, a, and_5_out, and_6_out, and_7_out, and_8_out);
  or or_5 (se, and_9_out, and_10_out);
  or or_6 (sf, a, and_11_out, and_12_out, and_13_out);

  assign sg = 1'b0;
endmodule

module display (
  input  Input_1,
  input  Input_2,
  input  Input_3,
  input  Input_4
);

  wire SevenSeg_1_sa, SevenSeg_1_sb, SevenSeg_1_sc, SevenSeg_1_sd, SevenSeg_1_se, SevenSeg_1_sf,
       SevenSeg_1_sg;

  SevenSeg SevenSeg_1 (
    .a(Input_1), .b(Input_2), .c(Input_3), .d(Input_4), .sa(SevenSeg_1_sa), .sb(SevenSeg_1_sb),
    .sc(SevenSeg_1_sc), .sd(SevenSeg_1_sd), .se(SevenSeg_1_se), .sf(SevenSeg_1_sf), .sg(SevenSeg_1_sg));
  _7_Segment_Display L_7_Segment_Display_1 (
    .g(SevenSeg_1_sg), .f(SevenSeg_1_sf), .a(SevenSeg_1_sa), .b(SevenSeg_1_sb), .e(SevenSeg_1_se),
    .d(SevenSeg_1_sd), .c(SevenSeg_1_sc));  // open: dp
endmodule
